# Fritzing sketch technisch_model (saved by Fritzing 0.9.3b)
breadboards: 2

parts:
  Raspberry_Pi_1 = Raspberry Pi 3 [part_number=RPI-3-V1.2]
  MOTOR1 = 28BYJ-48 Stepper Motor
  X1 = X113647 Stepper Driver Board [package=board]
  MOTOR2 = 28BYJ-48 Stepper Motor
  X2 = X113647 Stepper Driver Board [package=board]
  Onderdeel1 = SRF05 Ultrasonic Rangefinder
  R1 = Resistor [tolerance=±5% resistance=330 package=THT]
  R2 = Resistor [tolerance=±5% resistance=470 package=THT]

nets:
  N1: Raspberry_Pi_1.GPIO6, X1.IN1
  N2: Raspberry_Pi_1.GPIO13, X1.IN2
  N3: Raspberry_Pi_1.GPIO19, X1.IN3
  N4: Raspberry_Pi_1.GPIO26, X1.IN4
  N5: Raspberry_Pi_1.GPIO21, X2.IN4
  N6: Raspberry_Pi_1.GPIO20, X2.IN3
  N7: Raspberry_Pi_1.GPIO16, X2.IN2
  N8: Raspberry_Pi_1.GPIO12, X2.IN1
  N9: Raspberry_Pi_1.GPIO24, R1.Pin_1, R2.Pin_1
  N10: Raspberry_Pi_1.GPIO23, Onderdeel1.Echo
  GND: Raspberry_Pi_1.GND, X1.GND, X2.GND, Onderdeel1.GND
  5V: Raspberry_Pi_1.5V, X1.+V, X2.+V, Onderdeel1.VCC, R2.Pin_0
  N11: MOTOR1.BLUE, X1.BLUE
  N12: MOTOR1.PINK, X1.PINK
  N13: MOTOR1.RED, X1.RED
  N14: MOTOR1.ORANGE, X1.ORANGE
  N15: MOTOR1.YELLOW, X1.YELLOW
  N16: MOTOR2.BLUE, X2.BLUE
  N17: MOTOR2.PINK, X2.PINK
  N18: MOTOR2.RED, X2.RED
  N19: MOTOR2.ORANGE, X2.ORANGE
  N20: MOTOR2.YELLOW, X2.YELLOW
  N21: Onderdeel1.Trig, R1.Pin_0

custom parts:
  28BYJ-48 Stepper Motor: 28BYJ-48 gear-reduction stepper motor (small)
  X113647 Stepper Driver Board: A common stepper motor driver board based on ULN2003APG darlington array
